// Logisim project DataBridge.circ as structural Verilog: 1 circuit, main circuit main
module main (
  input  dv_bit,
  input  DataOut,
  output dl_bit
);

  wire transistor_2_out, transistor_3_out;

  Transistor #(.\type ("n")) transistor_1 (.in(transistor_2_out), .out(dl_bit), .gate(transistor_3_out));
  Transistor #(.\type ("n")) transistor_2 (.in(1'b0), .out(transistor_2_out), .gate(DataOut));
  Transistor #(.\type ("n")) transistor_3 (.in(1'b0), .out(transistor_3_out), .gate(dv_bit));
  Transistor transistor_4 (.in(1'b1), .out(transistor_3_out), .gate(dv_bit));
endmodule
