// Logisim project DataLatch.circ as structural Verilog: 2 circuits, main circuit main
module main (
  input  CLK,
  input  Test1,
  input  ExtDB_in,
  input  IntDB_in,
  input  Res_to_DL,
  input  Res_in,
  output ExtDB_out,
  output IntDB_out
);

  wire and_1_out, dlatch_1_q, dlatch_2_q, multiplexer_1_out, nor_1_out, nor_2_out, nor_3_out, not_1_out,
       not_2_out, or_1_out, undriven;

  or or_1 (or_1_out, Test1, CLK);
  // NoConnect on undriven
  DLatch dlatch_1 (.d(ExtDB_in), .q(dlatch_1_q));  // open: nq
  nor nor_1 (nor_1_out, Test1, dlatch_2_q);
  DLatch dlatch_2 (.d(IntDB_in), .q(dlatch_2_q));  // open: nq
  Multiplexer multiplexer_1 (.in0(1'b1), .in1(undriven), .out(multiplexer_1_out), .sel(or_1_out));
  nor nor_2 (nor_2_out, Test1, dlatch_1_q);
  not not_1 (not_1_out, Res_in);
  Multiplexer multiplexer_2 (.in0(multiplexer_1_out), .in1(1'b0), .out(ExtDB_out), .sel(nor_1_out));
  nor nor_3 (nor_3_out, nor_2_out, and_1_out);
  and and_1 (and_1_out, Res_to_DL, not_1_out);
  not not_2 (not_2_out, and_1_out);
  Multiplexer multiplexer_3 (.in0(not_2_out), .in1(nor_3_out), .out(IntDB_out), .sel(CLK));

  // Notes on the sheet:
  //   CLK=0: Int bus -> Ext bus
  //   CLK=1: Ext bus / Res -> Int bus
endmodule

module DLatch (
  input  d,
  output q,
  output nq
);

  D_Flip_Flop #(.trigger("high")) d_ff_1 (.D(d), .clk(1'b1), .Q(q), .Qn(nq));  // open: preset, reset
endmodule
