// Logisim project DataMux.circ as structural Verilog: 2 circuits, main circuit main
module main (
  input  CLK,
  input  Test1,
  input  ExtDB_in,
  input  Res_to_DL,
  input  Res_in,
  input  DataOut,
  input  DV,
  input  IntDB_in,
  output IntDB_out,
  output ExtDB_out
);

  wire controlled_buffer_1_out, ext_to_int_q, int_to_ext_q, multiplexer_1_out, multiplexer_2_out,
       multiplexer_4_out, not_1_out;

  not not_1 (not_1_out, Test1);
  assign controlled_buffer_1_out = not_1_out ? ext_to_int_q : 1'bz;  // Controlled_Buffer controlled_buffer_1
  DLatch ext_to_int (.d(ExtDB_in), .q(ext_to_int_q));  // open: nq
  DLatch int_to_ext (.d(IntDB_in), .q(int_to_ext_q));  // open: nq
  Multiplexer multiplexer_1 (.in0(1'b1), .in1(controlled_buffer_1_out), .out(multiplexer_1_out), .sel(CLK));
  Multiplexer multiplexer_2 (.in0(multiplexer_1_out), .in1(Res_in), .out(multiplexer_2_out), .sel(Res_to_DL));
  Multiplexer multiplexer_3 (.in0(multiplexer_2_out), .in1(DV), .out(IntDB_out), .sel(DataOut));
  Multiplexer multiplexer_4 (.in0(1'b1), .in1(int_to_ext_q), .out(multiplexer_4_out), .sel(CLK));
  assign ExtDB_out = not_1_out ? multiplexer_4_out : 1'bz;  // Controlled_Buffer controlled_buffer_2

  // Notes on the sheet:
  //   CLK2
  //   Maybe1
  //   D
  //   s3_oe_alu_to_pbus
  //   s3_oe_rbus_to_pbus
  //   DL
  //   DL
  //   D
endmodule

module DLatch (
  input  d,
  output q,
  output nq
);

  D_Flip_Flop #(.trigger("high")) d_ff_1 (.D(d), .clk(1'b1), .Q(q), .Qn(nq));  // open: preset, reset
endmodule
