// Logisim project IncDec.circ as structural Verilog: 5 circuits, main circuit Top
module Top (
  input  TTB1,
  input  TTB2,
  input  TTB3
);

  wire CLK4_out;
  wire [7:0] incdec_1_n_res_hi, incdec_1_n_res_lo;
  wire [15:0] not_1_out, not_2_out, register_1_q;

  Clock CLK4 (.out(CLK4_out));
  Register #(.trigger("falling"), .width(16)) register_1 (
    .D(not_2_out), .en(1'b1), .clk(CLK4_out), .Q(register_1_q));  // open: clr
  assign not_1_out = ~register_1_q;  // NOT_Gate not_1, 16 bits wide
  IncDec incdec_1 (
    .CLK4(CLK4_out), .TTB1(TTB1), .TTB2(TTB2), .TTB3(TTB3), .n_val_lo(not_1_out[7:0]),
    .n_val_hi(not_1_out[15:8]), .n_res_lo(incdec_1_n_res_lo), .n_res_hi(incdec_1_n_res_hi));
  assign not_2_out = ~{incdec_1_n_res_hi, incdec_1_n_res_lo};  // NOT_Gate not_2, 16 bits wide
endmodule

module IncDec (
  input  CLK4,
  input  TTB1,
  input  TTB2,
  input  TTB3,
  input  [7:0] n_val_lo,
  input  [7:0] n_val_hi,
  output [7:0] n_res_lo,
  output [7:0] n_res_hi
);

  wire [7:0] carry_chain_1_xa_hi, carry_chain_1_xa_lo, cntbit_1_cout, cntbit_9_cout;

  cntbit cntbit_1 (
    .n_val_in(n_val_lo[0]), .cin(carry_chain_1_xa_lo[0]), .TTB3(TTB3), .TTB2(TTB2), .n_val_out(n_res_lo[0]),
    .cout(cntbit_1_cout[0]));
  cntbit cntbit_2 (
    .n_val_in(n_val_lo[1]), .cin(carry_chain_1_xa_lo[1]), .TTB3(TTB3), .TTB2(TTB2), .n_val_out(n_res_lo[1]),
    .cout(cntbit_1_cout[1]));
  cntbit cntbit_3 (
    .n_val_in(n_val_lo[2]), .cin(carry_chain_1_xa_lo[2]), .TTB3(TTB3), .TTB2(TTB2), .n_val_out(n_res_lo[2]),
    .cout(cntbit_1_cout[2]));
  cntbit cntbit_4 (
    .n_val_in(n_val_lo[3]), .cin(carry_chain_1_xa_lo[3]), .TTB3(TTB3), .TTB2(TTB2), .n_val_out(n_res_lo[3]),
    .cout(cntbit_1_cout[3]));
  cntbit cntbit_5 (
    .n_val_in(n_val_lo[4]), .cin(carry_chain_1_xa_lo[4]), .TTB3(TTB3), .TTB2(TTB2), .n_val_out(n_res_lo[4]),
    .cout(cntbit_1_cout[4]));
  cntbit cntbit_6 (
    .n_val_in(n_val_lo[5]), .cin(carry_chain_1_xa_lo[5]), .TTB3(TTB3), .TTB2(TTB2), .n_val_out(n_res_lo[5]),
    .cout(cntbit_1_cout[5]));
  cntbit cntbit_7 (
    .n_val_in(n_val_lo[6]), .cin(carry_chain_1_xa_lo[6]), .TTB3(TTB3), .TTB2(TTB2), .n_val_out(n_res_lo[6]),
    .cout(cntbit_1_cout[6]));
  cntbit cntbit_8 (
    .n_val_in(n_val_lo[7]), .cin(carry_chain_1_xa_lo[7]), .TTB3(TTB3), .TTB2(TTB2), .n_val_out(n_res_lo[7]),
    .cout(cntbit_1_cout[7]));
  carry_chain carry_chain_1 (
    .CLK4(CLK4), .mq_lo(cntbit_1_cout), .TTB1(TTB1), .TTB2(TTB2), .TTB3(TTB3), .mq_hi(cntbit_9_cout),
    .xa_lo(carry_chain_1_xa_lo), .xa_hi(carry_chain_1_xa_hi));
  cntbit cntbit_9 (
    .n_val_in(n_val_hi[0]), .cin(carry_chain_1_xa_hi[0]), .TTB3(TTB3), .TTB2(TTB2), .n_val_out(n_res_hi[0]),
    .cout(cntbit_9_cout[0]));
  cntbit cntbit_10 (
    .n_val_in(n_val_hi[1]), .cin(carry_chain_1_xa_hi[1]), .TTB3(TTB3), .TTB2(TTB2), .n_val_out(n_res_hi[1]),
    .cout(cntbit_9_cout[1]));
  cntbit cntbit_11 (
    .n_val_in(n_val_hi[2]), .cin(carry_chain_1_xa_hi[2]), .TTB3(TTB3), .TTB2(TTB2), .n_val_out(n_res_hi[2]),
    .cout(cntbit_9_cout[2]));
  cntbit cntbit_12 (
    .n_val_in(n_val_hi[3]), .cin(carry_chain_1_xa_hi[3]), .TTB3(TTB3), .TTB2(TTB2), .n_val_out(n_res_hi[3]),
    .cout(cntbit_9_cout[3]));
  cntbit cntbit_13 (
    .n_val_in(n_val_hi[4]), .cin(carry_chain_1_xa_hi[4]), .TTB3(TTB3), .TTB2(TTB2), .n_val_out(n_res_hi[4]),
    .cout(cntbit_9_cout[4]));
  cntbit cntbit_14 (
    .n_val_in(n_val_hi[5]), .cin(carry_chain_1_xa_hi[5]), .TTB3(TTB3), .TTB2(TTB2), .n_val_out(n_res_hi[5]),
    .cout(cntbit_9_cout[5]));
  cntbit cntbit_15 (
    .n_val_in(n_val_hi[6]), .cin(carry_chain_1_xa_hi[6]), .TTB3(TTB3), .TTB2(TTB2), .n_val_out(n_res_hi[6]),
    .cout(cntbit_9_cout[6]));
  cntbit cntbit_16 (
    .n_val_in(n_val_hi[7]), .cin(carry_chain_1_xa_hi[7]), .TTB3(TTB3), .TTB2(TTB2), .n_val_out(n_res_hi[7]),
    .cout(cntbit_9_cout[7]));

  // Notes on the sheet:
  //   ~cbus
  //   ~dbus
  //   A0-A7
  //   A8-A15
  //   adl
  //   adh
endmodule

module cntbit (
  input  n_val_in,
  input  cin,
  input  TTB3,
  input  TTB2,
  output n_val_out,
  output cout
);

  wire multiplexer_1_out, not_1_out, not_2_out, not_3_out;

  xor xor_1 (n_val_out, n_val_in, cin);
  not not_1 (not_1_out, n_val_in);
  not not_2 (not_2_out, TTB3);
  Multiplexer multiplexer_1 (.in0(not_2_out), .in1(not_3_out), .out(multiplexer_1_out), .sel(not_1_out));
  not not_3 (not_3_out, TTB2);
  not not_4 (cout, multiplexer_1_out);
endmodule

module carry_chain (
  input  CLK4,
  input  [7:0] mq_lo,
  input  TTB1,
  input  TTB2,
  input  TTB3,
  input  [7:0] mq_hi,
  output [7:0] xa_lo,
  output [7:0] xa_hi
);

  wire transistor_1_out, transistor_2_out, transistor_3_out, transistor_4_out, transistor_6_out,
       transistor_8_out, transistor_9_out, transistor_13_out, transistor_15_out, transistor_16_out,
       transistor_19_out, transistor_20_out, transistor_23_out, transistor_24_out, transistor_27_out,
       transistor_28_out, transistor_31_out, transistor_32_out;

  Transistor #(.\type ("n")) transistor_1 (.in(transistor_2_out), .out(transistor_1_out), .gate(mq_lo[7]));
  Transistor #(.\type ("n")) transistor_2 (.in(1'b0), .out(transistor_2_out), .gate(CLK4));
  Transistor transistor_3 (.in(1'b1), .out(transistor_3_out), .gate(CLK4));
  Transistor #(.\type ("n")) transistor_4 (.in(1'b0), .out(transistor_4_out), .gate(CLK4));
  Transistor #(.\type ("n")) transistor_5 (.in(transistor_4_out), .out(transistor_3_out), .gate(mq_lo[0]));
  // NoConnect on mq_hi[7]
  Transistor #(.\type ("n")) transistor_6 (.in(transistor_1_out), .out(transistor_6_out), .gate(xa_lo[7]));
  Transistor #(.\type ("n")) transistor_7 (.in(transistor_2_out), .out(transistor_6_out), .gate(TTB1));
  Transistor transistor_8 (.in(1'b1), .out(transistor_8_out), .gate(CLK4));
  Transistor transistor_9 (.in(1'b1), .out(transistor_9_out), .gate(CLK4));
  Transistor #(.\type ("n")) transistor_10 (.in(transistor_3_out), .out(transistor_8_out), .gate(mq_lo[1]));
  Transistor #(.\type ("n")) transistor_11 (.in(transistor_8_out), .out(transistor_9_out), .gate(mq_lo[2]));
  Transistor transistor_12 (.in(1'b1), .out(transistor_6_out), .gate(CLK4));
  Transistor transistor_13 (.in(1'b1), .out(transistor_13_out), .gate(CLK4));
  Transistor #(.\type ("n")) transistor_14 (.in(transistor_6_out), .out(transistor_13_out), .gate(mq_hi[0]));
  Transistor transistor_15 (.in(1'b1), .out(transistor_15_out), .gate(CLK4));
  Transistor transistor_16 (.in(1'b1), .out(transistor_16_out), .gate(CLK4));
  Transistor #(.\type ("n")) transistor_17 (.in(transistor_9_out), .out(transistor_15_out), .gate(mq_lo[3]));
  Transistor #(.\type ("n")) transistor_18 (.in(transistor_15_out), .out(transistor_16_out), .gate(mq_lo[4]));
  Transistor transistor_19 (.in(1'b1), .out(transistor_19_out), .gate(CLK4));
  Transistor transistor_20 (.in(1'b1), .out(transistor_20_out), .gate(CLK4));
  Transistor #(.\type ("n")) transistor_21 (.in(transistor_13_out), .out(transistor_19_out), .gate(mq_hi[1]));
  Transistor #(.\type ("n")) transistor_22 (.in(transistor_19_out), .out(transistor_20_out), .gate(mq_hi[2]));
  Transistor transistor_23 (.in(1'b1), .out(transistor_23_out), .gate(CLK4));
  Transistor transistor_24 (.in(1'b1), .out(transistor_24_out), .gate(CLK4));
  Transistor #(.\type ("n")) transistor_25 (.in(transistor_16_out), .out(transistor_23_out), .gate(mq_lo[5]));
  Transistor #(.\type ("n")) transistor_26 (.in(transistor_23_out), .out(transistor_24_out), .gate(mq_lo[6]));
  or or_1 (xa_lo[0], TTB2, TTB3);
  Transistor transistor_27 (.in(1'b1), .out(transistor_27_out), .gate(CLK4));
  Transistor transistor_28 (.in(1'b1), .out(transistor_28_out), .gate(CLK4));
  Transistor #(.\type ("n")) transistor_29 (.in(transistor_20_out), .out(transistor_27_out), .gate(mq_hi[3]));
  Transistor #(.\type ("n")) transistor_30 (.in(transistor_27_out), .out(transistor_28_out), .gate(mq_hi[4]));
  Transistor transistor_31 (.in(1'b1), .out(transistor_31_out), .gate(CLK4));
  Transistor transistor_32 (.in(1'b1), .out(transistor_32_out), .gate(CLK4));
  Transistor #(.\type ("n")) transistor_33 (.in(transistor_28_out), .out(transistor_31_out), .gate(mq_hi[5]));
  Transistor #(.\type ("n")) transistor_34 (.in(transistor_31_out), .out(transistor_32_out), .gate(mq_hi[6]));
  DLatch dlatch_1 (.d(transistor_24_out), .nq(xa_lo[7]));  // open: q
  DLatch dlatch_2 (.d(transistor_23_out), .nq(xa_lo[6]));  // open: q
  DLatch dlatch_3 (.d(transistor_16_out), .nq(xa_lo[5]));  // open: q
  DLatch dlatch_4 (.d(transistor_15_out), .nq(xa_lo[4]));  // open: q
  DLatch dlatch_5 (.d(transistor_9_out), .nq(xa_lo[3]));  // open: q
  DLatch dlatch_6 (.d(transistor_8_out), .nq(xa_lo[2]));  // open: q
  DLatch dlatch_7 (.d(transistor_3_out), .nq(xa_lo[1]));  // open: q
  DLatch dlatch_8 (.d(transistor_32_out), .nq(xa_hi[7]));  // open: q
  DLatch dlatch_9 (.d(transistor_31_out), .nq(xa_hi[6]));  // open: q
  DLatch dlatch_10 (.d(transistor_28_out), .nq(xa_hi[5]));  // open: q
  DLatch dlatch_11 (.d(transistor_27_out), .nq(xa_hi[4]));  // open: q
  DLatch dlatch_12 (.d(transistor_20_out), .nq(xa_hi[3]));  // open: q
  DLatch dlatch_13 (.d(transistor_19_out), .nq(xa_hi[2]));  // open: q
  DLatch dlatch_14 (.d(transistor_13_out), .nq(xa_hi[1]));  // open: q
  DLatch dlatch_15 (.d(transistor_6_out), .nq(xa_hi[0]));  // open: q

  // Notes on the sheet:
  //   carry_in [7:0]
  //   carry_in [15:8]
  //   cin[7]
  //   cout[7]
  //   DLatch implemented as `not` (FET gate mem)
  //   carry_out [7:0]
  //   carry_out [15:8]
endmodule

module DLatch (
  input  d,
  output q,
  output nq
);

  D_Flip_Flop #(.trigger("high")) d_ff_1 (.D(d), .clk(1'b1), .Q(q), .Qn(nq));  // open: preset, reset
endmodule
