// Logisim project module5.circ as structural Verilog: 5 circuits, main circuit main
module main (
  input  ALU_to_top,
  input  [3:0] m,
  input  [3:0] h,
  output [3:0] C1_4
);

  Carry1_Gen carry1_gen_1 (.CarryIn(ALU_to_top), .G(m), .P(h), .C1(C1_4[0]));
  Carry2_Gen carry2_gen_1 (.CarryIn(ALU_to_top), .G(m), .P(h), .C2(C1_4[1]));
  Carry3_Gen carry3_gen_1 (.CarryIn(ALU_to_top), .G(m), .P(h), .C3(C1_4[2]));
  Carry4_Gen carry4_gen_1 (.CarryIn(ALU_to_top), .G(m), .P(h), .C4(C1_4[3]));

  // Notes on the sheet:
  //   require not
endmodule

module Carry1_Gen (
  input  CarryIn,
  input  [3:0] G,
  input  [3:0] P,
  output C1
);

  wire transistor_1_out, transistor_2_out, transistor_3_out, transistor_5_out;

  Transistor #(.\type ("n")) transistor_1 (.in(1'b0), .out(transistor_1_out), .gate(G[0]));
  Transistor transistor_2 (.in(1'b1), .out(transistor_2_out), .gate(P[0]));
  Transistor #(.\type ("n")) transistor_3 (.in(1'b0), .out(transistor_3_out), .gate(P[0]));
  Transistor #(.\type ("n")) transistor_4 (.in(transistor_3_out), .out(transistor_1_out), .gate(CarryIn));
  Transistor transistor_5 (.in(1'b1), .out(transistor_5_out), .gate(G[0]));
  Transistor transistor_6 (.in(transistor_5_out), .out(transistor_2_out), .gate(CarryIn));
  Pull_Resistor #(.pull(1)) pull_resistor_1 (.node(transistor_1_out));
  and and_1 (C1, transistor_1_out, transistor_2_out);
  Pull_Resistor pull_resistor_2 (.node(transistor_2_out));
endmodule

module Carry2_Gen (
  input  CarryIn,
  input  [3:0] G,
  input  [3:0] P,
  output C2
);

  wire transistor_1_out, transistor_2_out, transistor_3_out, transistor_4_out, transistor_7_out,
       transistor_8_out;

  Transistor #(.\type ("n")) transistor_1 (.in(1'b0), .out(transistor_1_out), .gate(G[1]));
  Transistor transistor_2 (.in(1'b1), .out(transistor_2_out), .gate(P[1]));
  Transistor #(.\type ("n")) transistor_3 (.in(1'b0), .out(transistor_3_out), .gate(P[1]));
  Transistor transistor_4 (.in(1'b1), .out(transistor_4_out), .gate(G[1]));
  Transistor #(.\type ("n")) transistor_5 (.in(transistor_3_out), .out(transistor_1_out), .gate(G[0]));
  Transistor transistor_6 (.in(transistor_4_out), .out(transistor_2_out), .gate(P[0]));
  Transistor #(.\type ("n")) transistor_7 (.in(transistor_3_out), .out(transistor_7_out), .gate(P[0]));
  Transistor transistor_8 (.in(transistor_4_out), .out(transistor_8_out), .gate(G[0]));
  Transistor #(.\type ("n")) transistor_9 (.in(transistor_7_out), .out(transistor_1_out), .gate(CarryIn));
  Pull_Resistor #(.pull(1)) pull_resistor_1 (.node(transistor_1_out));
  Transistor transistor_10 (.in(transistor_8_out), .out(transistor_2_out), .gate(CarryIn));
  Pull_Resistor pull_resistor_2 (.node(transistor_2_out));
  and and_1 (C2, transistor_1_out, transistor_2_out);
endmodule

module Carry3_Gen (
  input  CarryIn,
  input  [3:0] G,
  input  [3:0] P,
  output C3
);

  wire transistor_1_out, transistor_2_out, transistor_3_out, transistor_4_out, transistor_7_out,
       transistor_8_out, transistor_11_out, transistor_13_out;

  Transistor #(.\type ("n")) transistor_1 (.in(1'b0), .out(transistor_1_out), .gate(G[2]));
  Transistor transistor_2 (.in(1'b1), .out(transistor_2_out), .gate(P[2]));
  Transistor #(.\type ("n")) transistor_3 (.in(1'b0), .out(transistor_3_out), .gate(P[2]));
  Transistor transistor_4 (.in(1'b1), .out(transistor_4_out), .gate(G[2]));
  Transistor #(.\type ("n")) transistor_5 (.in(transistor_3_out), .out(transistor_1_out), .gate(G[1]));
  Transistor transistor_6 (.in(transistor_4_out), .out(transistor_2_out), .gate(P[1]));
  Transistor #(.\type ("n")) transistor_7 (.in(transistor_3_out), .out(transistor_7_out), .gate(P[1]));
  Transistor transistor_8 (.in(transistor_4_out), .out(transistor_8_out), .gate(G[1]));
  Transistor #(.\type ("n")) transistor_9 (.in(transistor_7_out), .out(transistor_1_out), .gate(G[0]));
  Transistor transistor_10 (.in(transistor_8_out), .out(transistor_2_out), .gate(P[0]));
  Transistor #(.\type ("n")) transistor_11 (.in(transistor_7_out), .out(transistor_11_out), .gate(P[0]));
  Transistor #(.\type ("n")) transistor_12 (.in(transistor_11_out), .out(transistor_1_out), .gate(CarryIn));
  Transistor transistor_13 (.in(transistor_8_out), .out(transistor_13_out), .gate(G[0]));
  Transistor transistor_14 (.in(transistor_13_out), .out(transistor_2_out), .gate(CarryIn));
  Pull_Resistor #(.pull(1)) pull_resistor_1 (.node(transistor_1_out));
  Pull_Resistor pull_resistor_2 (.node(transistor_2_out));
  and and_1 (C3, transistor_1_out, transistor_2_out);
endmodule

module Carry4_Gen (
  input  CarryIn,
  input  [3:0] G,
  input  [3:0] P,
  output C4
);

  wire transistor_1_out, transistor_2_out, transistor_3_out, transistor_4_out, transistor_7_out,
       transistor_8_out, transistor_11_out, transistor_12_out, transistor_15_out, transistor_16_out;

  Transistor #(.\type ("n")) transistor_1 (.in(1'b0), .out(transistor_1_out), .gate(G[3]));
  Transistor transistor_2 (.in(1'b1), .out(transistor_2_out), .gate(P[3]));
  Transistor #(.\type ("n")) transistor_3 (.in(1'b0), .out(transistor_3_out), .gate(P[3]));
  Transistor transistor_4 (.in(1'b1), .out(transistor_4_out), .gate(G[3]));
  Transistor #(.\type ("n")) transistor_5 (.in(transistor_3_out), .out(transistor_1_out), .gate(G[2]));
  Transistor transistor_6 (.in(transistor_4_out), .out(transistor_2_out), .gate(P[2]));
  Transistor #(.\type ("n")) transistor_7 (.in(transistor_3_out), .out(transistor_7_out), .gate(P[2]));
  Transistor transistor_8 (.in(transistor_4_out), .out(transistor_8_out), .gate(G[2]));
  Transistor #(.\type ("n")) transistor_9 (.in(transistor_7_out), .out(transistor_1_out), .gate(G[1]));
  Transistor transistor_10 (.in(transistor_8_out), .out(transistor_2_out), .gate(P[1]));
  Transistor #(.\type ("n")) transistor_11 (.in(transistor_7_out), .out(transistor_11_out), .gate(P[1]));
  Transistor transistor_12 (.in(transistor_8_out), .out(transistor_12_out), .gate(G[1]));
  Transistor #(.\type ("n")) transistor_13 (.in(transistor_11_out), .out(transistor_1_out), .gate(G[0]));
  Transistor transistor_14 (.in(transistor_12_out), .out(transistor_2_out), .gate(P[0]));
  Transistor #(.\type ("n")) transistor_15 (.in(transistor_11_out), .out(transistor_15_out), .gate(P[0]));
  Transistor transistor_16 (.in(transistor_12_out), .out(transistor_16_out), .gate(G[0]));
  Transistor #(.\type ("n")) transistor_17 (.in(transistor_15_out), .out(transistor_1_out), .gate(CarryIn));
  Pull_Resistor #(.pull(1)) pull_resistor_1 (.node(transistor_1_out));
  Transistor transistor_18 (.in(transistor_16_out), .out(transistor_2_out), .gate(CarryIn));
  Pull_Resistor pull_resistor_2 (.node(transistor_2_out));
  and and_1 (C4, transistor_1_out, transistor_2_out);
endmodule
