// Logisim project seq.circ as structural Verilog: 6 circuits, main circuit main
module main (
  input  ALU_Out1,
  input  Maybe1,
  input  nCLK4,
  input  CLK9,
  input  CLK8,
  input  NMI,
  input  MMIO_REQ,
  input  CLK6,
  input  IPL_REQ,
  input  Maybe2,
  input  CLK4,
  input  SeqControl_2,
  input  CLK2,
  input  CLK1,
  input  SYNC_RESET,
  input  SeqControl_1,
  input  RESET,
  input  x41,
  input  [7:0] IR,
  input  OSC_STABLE,
  input  WAKE,
  input  d93,
  input  d99,
  input  d100,
  input  d101,
  input  d102,
  input  w6,
  input  w11,
  input  w18,
  input  w20,
  input  w26,
  input  w32,
  input  w33,
  input  w40,
  output a20,
  output a21,
  output a22,
  output a23,
  output a24,
  output a25,
  output MREQ,
  output RD,
  output a3,
  output a1,
  output CLK_ENA,
  output SeqOut_2,
  output SeqOut_1,
  output OSC_ENA
);

  wire and_1_out, and_2_out, and_3_out, and_4_out, and_5_out, and_6_out, and_7_out, g18_out, g19_out,
       g20_out, g21_out, g22_out, g23_out, g24_out, g25_out, g28_out, g29_out, g32_out, g33_q, g34_out,
       g35_q, g36_q, g37_q, g40_out, g41_out, g42_q, g44_out, g45_out, g46_q, g47_out, g48_out, g49_q,
       g50_out, g51_out, g53_out, g54_q, g55_nq, g56_out, g57_q, g58_q, g59_out, g60_out, g62_q, g63_q,
       g64_out, g65_out, g66_out, g68_q, g69_out, g70_out, g71_q, g72_x, g74_q, g75_out, g76_out, g77_q,
       g78_out, g79_out, g80_out, g81_out, g82_out, g83_out, g84_q, g86_out, g87_out, g88_out, g89_q,
       g90_out, g92_q, g93_out, g94_q, g95_out, g96_out, g97_out, multiplexer_1_out, multiplexer_2_out,
       nand_1_out, nand_2_out, nor_1_out, nor_2_out, nor_3_out, nor_4_out, nor_5_out, not_1_out, or_1_out,
       or_2_out;

  not g53 (g53_out, NMI);
  dff g54 (.ck(CLK9), .cck(CLK8), .d(g53_out), .q(g54_q));
  nor g50 (g50_out, g49_q, SYNC_RESET, 1'b0);
  not g51 (g51_out, g50_out);
  latch g55 (.clk(CLK8), .cclk(CLK9), .d(g54_q), .nq(g55_nq));
  not g41 (g41_out, d102);
  and and_1 (and_1_out, g41_out, w26, CLK4);
  and and_2 (and_2_out, SeqOut_1, d93);
  nor g87 (g87_out, SYNC_RESET, x41);
  nor g56 (g56_out, g55_nq, g53_out);
  nor nor_1 (nor_1_out, and_1_out, g51_out);
  nor nor_2 (nor_2_out, and_2_out, SYNC_RESET);
  not g86 (g86_out, g68_q);
  not g88 (g88_out, g87_out);
  not g40 (g40_out, nor_1_out);
  rs g71 (.nr(nor_2_out), .s(g56_out), .q(g71_q));
  rs g89 (.nr(g86_out), .s(g88_out), .q(g89_q));
  nand g70 (g70_out, g40_out, g94_q, g71_q);
  not g69 (g69_out, g70_out);
  dff g94 (.ck(CLK9), .cck(CLK8), .d(g89_q), .q(g94_q));
  and and_3 (and_3_out, g94_q, x41);
  and and_4 (and_4_out, d99, IR[3]);
  not g95 (g95_out, IR[3]);
  rs g68 (.nr(nor_2_out), .s(g69_out), .q(g68_q));
  nor nor_3 (nor_3_out, and_3_out, and_4_out);
  Multiplexer multiplexer_1 (.in0(1'b1), .in1(nor_3_out), .out(multiplexer_1_out), .sel(CLK4));
  and and_5 (and_5_out, g74_q, g94_q);
  nor nor_4 (nor_4_out, and_5_out, and_6_out, SYNC_RESET);
  and and_6 (and_6_out, d99, g95_out);
  not not_1 (not_1_out, SYNC_RESET);
  Multiplexer multiplexer_2 (.in0(not_1_out), .in1(nor_4_out), .out(multiplexer_2_out), .sel(CLK4));
  not g93 (g93_out, multiplexer_1_out);
  rs g92 (.nr(multiplexer_2_out), .s(g93_out), .q(g92_q));
  nand g90 (g90_out, g92_q, g89_q);
  nand g80 (g80_out, g95_out, d99);
  not g66 (g66_out, SYNC_RESET);
  not g81 (g81_out, g80_out);
  nand g79 (g79_out, g40_out, SeqControl_2);
  not g82 (g82_out, CLK4);
  not g18 (g18_out, w32);
  not g20 (g20_out, w33);
  not g22 (g22_out, w20);
  nor g24 (g24_out, ALU_Out1, g51_out);
  dff g84 (.ck(CLK1), .cck(CLK2), .d(g90_out), .q(g84_q));
  nand g59 (g59_out, g66_out, OSC_STABLE);
  not g32 (g32_out, CLK6);
  not g34 (g34_out, w26);
  nor g78 (g78_out, d93, SYNC_RESET);
  nand g19 (g19_out, g18_out, g24_out);
  nand g21 (g21_out, g20_out, g24_out);
  nand g23 (g23_out, g22_out, g24_out);
  nor g25 (g25_out, Maybe1, nCLK4);
  latchr g33 (.clk(CLK6), .cclk(g32_out), .ld(w26), .nld(g34_out), .d(d102), .res(g49_q), .q(g33_q));
  nor g83 (g83_out, g79_out, g84_q, g82_out, g81_out);
  dff g58 (.ck(CLK9), .cck(CLK8), .d(g59_out), .q(g58_q));
  not g29 (g29_out, a21);
  dff g57 (.ck(CLK9), .cck(CLK8), .d(g58_q), .q(g57_q));
  nand g65 (g65_out, IR[4], d101);
  rs g77 (.nr(g78_out), .s(g83_out), .q(g77_q));
  or or_1 (or_1_out, w26, w18);
  and and_7 (and_7_out, g29_out, g33_q);
  nor g28 (g28_out, g74_q, g51_out, 1'b0);
  not g64 (g64_out, g65_out);
  dff g35 (.ck(CLK9), .cck(CLK8), .d(g19_out), .q(g35_q));
  dff g36 (.ck(CLK9), .cck(CLK8), .d(g21_out), .q(g36_q));
  dff g37 (.ck(CLK9), .cck(CLK8), .d(g23_out), .q(g37_q));
  nand nand_1 (nand_1_out, or_1_out, g25_out);
  nor nor_5 (nor_5_out, and_7_out, 1'b0);
  not g44 (g44_out, g57_q);
  nor g76 (g76_out, g77_q, g68_q);
  not g12 (a20, g35_q);
  not g13 (a21, a20);
  not g14 (a22, g36_q);
  not g15 (a23, a22);
  not g16 (a24, g37_q);
  not g17 (a25, a24);
  not g27 (RD, nand_1_out);
  not g10 (a3, nor_5_out);
  not g1 (a1, g28_out);
  dff g46 (.ck(CLK9), .cck(CLK8), .d(d100), .q(g46_q));
  dff g63 (.ck(CLK9), .cck(CLK8), .d(g64_out), .q(g63_q));
  not g75 (g75_out, g76_out);
  nor g45 (g45_out, g44_out, g58_q);
  nor g47 (g47_out, g46_q, g63_q, RESET);
  nor g97 (g97_out, SYNC_RESET, RESET);
  dff g42 (.ck(CLK9), .cck(CLK8), .d(SeqControl_1), .q(g42_q));
  not g48 (g48_out, g47_out);
  not g96 (g96_out, g97_out);
  or or_2 (or_2_out, g42_q, g45_out);
  nand nand_2 (nand_2_out, or_2_out, g97_out);
  dff g74 (.ck(CLK9), .cck(CLK8), .d(g75_out), .q(g74_q));
  nor g60 (g60_out, WAKE, g96_out);
  mreq_cell g72 (.a(MMIO_REQ), .b(IPL_REQ), .c(Maybe2), .d(w11), .x(g72_x));
  not g73 (MREQ, g72_x);
  rs g49 (.nr(nand_2_out), .s(g48_out), .q(g49_q));
  dff g38 (.ck(CLK9), .cck(CLK8), .d(w40), .q(SeqOut_2));
  dff g67 (.ck(CLK9), .cck(CLK8), .d(g68_q), .q(SeqOut_1));
  rs g62 (.nr(g60_out), .s(g63_q), .q(g62_q));
  not g31 (CLK_ENA, g49_q);
  not g61 (OSC_ENA, g62_q);

  // Notes on the sheet:
  //   [!] See g84
  //   ck
  //   cck
  //   ck
  //   cck
  //   s1_int_s110
  //   s2_wr
  //   s2_addr_valid
  //   s2_m1
  //   s2_state2_next
  //   s2_state1_next
  //   1: Bus disable
  //   /NMI
  //   s1_op_di_ei_s0xx
  //   s1_op_halt_s0xx
  //   s1_op_nop_stop_s0xx
  //   s1_op_cb_s0xx
  //   s2_data_fetch_cycle
  //   s2_state0_next
  //   CLK_DIS
  //   Some inputs are shorted out. This is fine, just like in a real chip.
  //   s3_op_reti_s011
  //   NMI Edge detect
  //   s1_op_cb_s0xx
  //   s2_m1
  //   clk_dis_or_sync_reset
  //   s1_int_s110
  //   g55 in opposite clk phase
  //   g39
  //   g52
  //   s1_op_di_ei_s0xx
  //   Interrupt sequence start
  //   Interrupt sequence end
  //   g94
  //   All DFFs are posedge, except g84
  //   g91
  //   [!] Non-demorganized circuit
  //   The decoder commands when to switch state.
  //   clk_dis_or_sync_reset
  //   s1_op_di_ei_s0xx
  //   [!]
  //   CLK2/1 are coupled by complement, converting this DFF to negedge.
  //   s2_state2_next
  //   s2_state1_next
  //   s2_state0_next
  //   s2_m1
  //   s1_op_cb_s0xx
  //   CLK_DIS
  //   s1_int_s110
  //   Clock Control (HALT, STOP processing)
  //   Sequence state & modes
  //   s2_m1
  //   s1_op_nop_stop_s0xx
  //   s2_data_fetch_cycle
  //   s1_op_halt_s0xx
  //   g26
  //   g30
  //   OSC_STABLE Edge detect
  //   dff_state2
  //   dff_state1
  //   dff_state0
  //   dff_halt
  //   dff_stop
  //   cb_mode
  //   intr_dispatch
  //   Extra decoder inputs
  //   #State2
  //   State2
  //   #State1
  //   State1
  //   #State0
  //   State0
  //   Extra decoder inputs
  //   s2_addr_valid
  //   g43
  //   CLK_DIS
  //   rs_clk_disable
endmodule

module dff (
  input  ck,
  input  cck,
  input  d,
  output q
);

  // NoConnect on cck
  D_Flip_Flop d_ff_1 (.D(d), .clk(ck), .Q(q));  // open: Qn, preset, reset
endmodule

module latch (
  input  clk,
  input  cclk,
  input  d,
  output nq
);

  wire d_ff_1_q;

  // NoConnect on cclk
  D_Flip_Flop #(.trigger("high")) d_ff_1 (.D(d), .clk(clk), .Q(d_ff_1_q), .Qn(nq));  // open: preset, reset
  // NoConnect on d_ff_1_q

  // Notes on the sheet:
  //   level-triggered
endmodule

module rs (
  input  nr,
  input  s,
  output q
);

  wire not_1_out;

  not not_1 (not_1_out, nr);
  D_Flip_Flop #(.trigger("high")) d_ff_1 (.Q(q), .preset(s), .reset(not_1_out));  // open: D, clk, Qn

  // Notes on the sheet:
  //   #reset has priority over set
endmodule

module latchr (
  input  clk,
  input  cclk,
  input  ld,
  input  nld,
  input  d,
  input  res,
  output q
);

  wire and_1_out;

  // NoConnect on cclk
  // NoConnect on nld
  and and_1 (and_1_out, clk, ld);
  D_Flip_Flop #(.trigger("high")) d_ff_1 (.D(d), .clk(and_1_out), .Q(q), .reset(res));  // open: Qn, preset

  // Notes on the sheet:
  //   active-high triggered
endmodule

module mreq_cell (
  input  a,
  input  b,
  input  c,
  input  d,
  output x
);

  wire and_1_out, nor_1_out, nor_2_out, not_1_out;

  not not_1 (not_1_out, a);
  and and_1 (and_1_out, not_1_out, c);
  nor nor_1 (nor_1_out, a, b);
  nor nor_2 (nor_2_out, and_1_out, nor_1_out);
  Multiplexer multiplexer_1 (.in0(1'b1), .in1(nor_2_out), .out(x), .sel(d));

  // Notes on the sheet:
  //   IPL_DISABLE (Maybe2)
  //   MMIO_REQ
  //   IPL_REQ
  //   s2_addr_valid
  //   Immediately after this cell is the extra inverter, to get the MREQ signal
  //   #MREQ
endmodule
