// Logisim project DataLatch.circ as structural Verilog: 2 circuits, main circuit main
module main (
  input  CLK,
  input  Test1,
  input  ExtDB_in,
  input  Res_to_DL,
  input  Res_in,
  input  IntDB_in,
  output IntDB_out,
  output ExtDB_out
);

  wire ext_to_int_q, int_to_ext_q, multiplexer_1_out, multiplexer_2_out, multiplexer_4_out, not_1_out,
       undriven;

  not not_1 (not_1_out, Test1);
  // NoConnect on undriven
  DLatch ext_to_int (.d(ExtDB_in), .q(ext_to_int_q));  // open: nq
  DLatch int_to_ext (.d(IntDB_in), .q(int_to_ext_q));  // open: nq
  Multiplexer multiplexer_1 (.in0(undriven), .in1(ext_to_int_q), .out(multiplexer_1_out), .sel(not_1_out));
  Multiplexer multiplexer_2 (.in0(1'b1), .in1(multiplexer_1_out), .out(multiplexer_2_out), .sel(CLK));
  Multiplexer multiplexer_3 (.in0(multiplexer_2_out), .in1(Res_in), .out(IntDB_out), .sel(Res_to_DL));
  Multiplexer multiplexer_4 (.in0(1'b1), .in1(int_to_ext_q), .out(multiplexer_4_out), .sel(CLK));
  assign ExtDB_out = not_1_out ? multiplexer_4_out : 1'bz;  // Controlled_Buffer controlled_buffer_1
endmodule

module DLatch (
  input  d,
  output q,
  output nq
);

  D_Flip_Flop #(.trigger("high")) d_ff_1 (.D(d), .clk(1'b1), .Q(q), .Qn(nq));  // open: preset, reset
endmodule
