// Logisim project alu_shifter.circ as structural Verilog: 2 circuits, main circuit main
module main (
  input  CLK2,
  input  x0,
  input  x1,
  input  x5,
  input  x6,
  input  x7,
  input  x8,
  input  x9,
  input  x16,
  input  bc1,
  input  [7:0] DV,
  output [7:0] ca
);

  wire and_1_out, and_2_out, and_3_out, and_4_out, and_5_out, and_6_out, and_7_out, and_8_out, and_9_out,
       and_10_out, and_11_out, and_12_out, and_13_out, and_14_out, and_15_out, and_16_out, and_17_out,
       and_18_out, and_19_out, and_20_out, and_21_out, and_22_out, and_23_out, and_24_out, and_25_out,
       and_26_out, and_27_out, nor_1_out, nor_2_out, nor_3_out, nor_4_out, nor_5_out, nor_6_out, nor_7_out,
       nor_8_out;

  and and_1 (and_1_out, x0, DV[6]);
  and and_2 (and_2_out, x7, DV[0]);
  and and_3 (and_3_out, x8, bc1);
  and and_4 (and_4_out, x9, DV[7]);
  and and_5 (and_5_out, x16, DV[3]);
  nor nor_1 (nor_1_out, and_1_out, and_2_out, and_3_out, and_4_out, and_5_out);
  Multiplexer multiplexer_1 (.in0(nor_1_out), .in1(1'b1), .out(ca[7]), .sel(CLK2));
  and and_6 (and_6_out, x0, DV[5]);
  and and_7 (and_7_out, x1, DV[7]);
  and and_8 (and_8_out, x16, DV[2]);
  nor nor_2 (nor_2_out, and_6_out, and_7_out, and_8_out);
  Multiplexer multiplexer_2 (.in0(nor_2_out), .in1(1'b1), .out(ca[6]), .sel(CLK2));
  and and_9 (and_9_out, x0, DV[4]);
  and and_10 (and_10_out, x1, DV[6]);
  and and_11 (and_11_out, x16, DV[1]);
  nor nor_3 (nor_3_out, and_9_out, and_10_out, and_11_out);
  Multiplexer multiplexer_3 (.in0(nor_3_out), .in1(1'b1), .out(ca[5]), .sel(CLK2));
  and and_12 (and_12_out, x0, DV[3]);
  and and_13 (and_13_out, x1, DV[5]);
  and and_14 (and_14_out, x16, DV[0]);
  nor nor_4 (nor_4_out, and_12_out, and_13_out, and_14_out);
  Multiplexer multiplexer_4 (.in0(nor_4_out), .in1(1'b1), .out(ca[4]), .sel(CLK2));
  and and_15 (and_15_out, x0, DV[2]);
  and and_16 (and_16_out, x1, DV[4]);
  and and_17 (and_17_out, x16, DV[7]);
  nor nor_5 (nor_5_out, and_15_out, and_16_out, and_17_out);
  Multiplexer multiplexer_5 (.in0(nor_5_out), .in1(1'b1), .out(ca[3]), .sel(CLK2));
  and and_18 (and_18_out, x0, DV[1]);
  and and_19 (and_19_out, x1, DV[3]);
  and and_20 (and_20_out, x16, DV[6]);
  nor nor_6 (nor_6_out, and_18_out, and_19_out, and_20_out);
  Multiplexer multiplexer_6 (.in0(nor_6_out), .in1(1'b1), .out(ca[2]), .sel(CLK2));
  and and_21 (and_21_out, x0, DV[0]);
  and and_22 (and_22_out, x1, DV[2]);
  and and_23 (and_23_out, x16, DV[5]);
  nor nor_7 (nor_7_out, and_21_out, and_22_out, and_23_out);
  Multiplexer multiplexer_7 (.in0(nor_7_out), .in1(1'b1), .out(ca[1]), .sel(CLK2));
  and and_24 (and_24_out, x1, DV[1]);
  and and_25 (and_25_out, x5, DV[7]);
  and and_26 (and_26_out, x6, bc1);
  and and_27 (and_27_out, x16, DV[4]);
  nor nor_8 (nor_8_out, and_24_out, and_25_out, and_26_out, and_27_out);
  Multiplexer multiplexer_8 (.in0(nor_8_out), .in1(1'b1), .out(ca[0]), .sel(CLK2));

  // Other names for the same wires on the sheet: s3_alu_rl = x6; s3_alu_rlc = x5; s3_alu_rotate_shift_left = x0;
  //   s3_alu_rotate_shift_right = x1; s3_alu_rr = x8; s3_alu_rrc = x7; s3_alu_sra = x9; s3_alu_swap = x16

  // Notes on the sheet:
  //   bit7
  //   msb
  //   comb1
  //   comb2
  //   bit6
  //   bit5
  //   comb2
  //   comb2
  //   bit4
  //   comb2
  //   bit3
  //   bit2
  //   comb2
  //   comb2
  //   bit1
  //   bit0
  //   lsb
  //   comb3
  //   active low
endmodule

module DLatch_x8 (
  input  [7:0] d,
  output [7:0] q,
  output [7:0] nq
);

  Register #(.trigger("high")) register_1 (.D(d), .en(1'b1), .clk(1'b1), .Q(q));  // open: clr
  assign nq = ~q;  // NOT_Gate not_1, 8 bits wide
endmodule
