// Logisim project cc_check.circ as structural Verilog: 1 circuit, main circuit main
module main (
  input  w0,
  input  bc1,
  input  bc3,
  input  [7:0] IR,
  output cond_ok
);

  wire and_1_out, and_2_out, and_3_out, and_4_out, or_1_out;

  and and_1 (and_1_out, bc1, ~IR[3], IR[4]);  // AND_Gate
  and and_2 (and_2_out, ~bc1, IR[3], IR[4]);  // AND_Gate
  and and_3 (and_3_out, ~bc3, IR[3], ~IR[4]);  // AND_Gate
  and and_4 (and_4_out, bc3, ~IR[3], ~IR[4]);  // AND_Gate
  or or_1 (or_1_out, and_1_out, and_2_out, and_3_out, and_4_out);
  nand nand_1 (cond_ok, w0, or_1_out);

  // Notes on the sheet:
  //   s2_cc_check
  //   Flag C
  //   Flag Z
  //   11000000 - RET NZ
  //   11001000 - RET Z
  //   11010000 - RET NC
  //   11011000 - RET C
  //   The dynamic part of the logic is not shown for simplification purposes
  //   ALU_Out1 = ~cond_ok
endmodule
