// Logisim project ck1_ck2_tran.circ as structural Verilog: 1 circuit, main circuit main
module main (
  input  osc_ena,
  input  CK1,
  output n_clk_in,
  output CK2
);

  wire multiplexer_1_out, not_1_out, not_2_out, transistor_2_out, transistor_4_out, undriven, undriven_2,
       undriven_3;

  Transistor transistor_1 (.in(1'b1), .out(n_clk_in), .gate(transistor_2_out));
  Transistor transistor_2 (.in(1'b1), .out(transistor_2_out), .gate(osc_ena));
  Transistor #(.\type ("n")) transistor_3 (.in(1'b0), .out(n_clk_in), .gate(transistor_2_out));
  Transistor transistor_4 (.in(1'b1), .out(transistor_4_out), .gate(osc_ena));
  Transistor #(.\type ("n")) transistor_5 (.in(1'b0), .out(transistor_4_out), .gate(osc_ena));
  Transistor transistor_6 (.in(CK1), .out(transistor_2_out), .gate(transistor_4_out));
  Transistor #(.\type ("n")) transistor_7 (.in(CK1), .out(transistor_2_out), .gate(osc_ena));
  not super_inv (CK2, transistor_2_out);
  Multiplexer multiplexer_1 (.in0(undriven_2), .in1(undriven_3), .out(multiplexer_1_out), .sel(undriven));
  not not_1 (not_1_out, multiplexer_1_out);
  not not_2 (not_2_out, multiplexer_1_out);

  // Notes on the sheet:
  //   ~
  //   ~
  //   osc_ena
  //   1'b1
  //   CK1
  //   n_clk_in (internal)
  //   CK2 (external)
endmodule
