// Logisim project dmglib.circ as structural Verilog
module dmg_cnt (
  input  clk,
  input  d,
  input  load,
  output q,
  output nq
);

  wire and_1_out, and_2_out, multiplexer_1_out, multiplexer_2_out, nor_1_out, nor_2_out, nor_3_out,
       nor_4_out, not_1_out;

  and and_1 (and_1_out, d, load);
  nor nor_1 (nor_1_out, load, multiplexer_1_out);
  nor nor_2 (nor_2_out, and_1_out, nor_1_out);
  Multiplexer multiplexer_1 (.in0(nor_2_out), .in1(not_1_out), .out(multiplexer_1_out), .sel(clk));
  Multiplexer multiplexer_2 (.in0(multiplexer_1_out), .in1(nor_4_out), .out(multiplexer_2_out), .sel(clk));
  not not_1 (not_1_out, multiplexer_2_out);
  and and_2 (and_2_out, d, load);
  nor nor_3 (nor_3_out, load, multiplexer_2_out);
  nor nor_4 (nor_4_out, and_2_out, nor_3_out);
  not not_2 (q, nor_4_out);
  not not_3 (nq, not_1_out);
endmodule
