// Logisim project sck_tran.circ as structural Verilog: 1 circuit, main circuit main
module main (
  input  n_sck_ena_pu,
  input  sck_pad_in,
  input  sck_clr,
  input  n_sck_set,
  output n_sck_frompad,
  output sck_pad_out
);

  wire controlled_buffer_1_out, g1_out, g2_out, g3_out, g4_out, pull_resistor_1_node, transistor_2_out,
       transistor_3_out, transistor_6_out, transistor_12_out, transistor_15_out, undriven;

  Transistor transistor_1 (.in(1'b1), .out(sck_pad_in), .gate(n_sck_ena_pu));
  Transistor transistor_2 (.in(1'b1), .out(transistor_2_out), .gate(sck_pad_in));
  Transistor transistor_3 (.in(1'b1), .out(transistor_3_out), .gate(transistor_6_out));
  Transistor transistor_4 (.in(1'b1), .out(n_sck_frompad), .gate(transistor_3_out));
  Transistor #(.\type ("n")) transistor_5 (.in(1'b0), .out(n_sck_frompad), .gate(transistor_3_out));
  Transistor transistor_6 (.in(1'b1), .out(transistor_6_out), .gate(sck_pad_in));
  Transistor transistor_7 (.in(1'b1), .out(transistor_2_out), .gate(transistor_3_out));
  Transistor transistor_8 (.in(1'b1), .out(transistor_3_out), .gate(transistor_2_out));
  Transistor #(.\type ("n")) transistor_9 (.in(transistor_12_out), .out(transistor_3_out), .gate(transistor_2_out));
  Transistor #(.\type ("n")) transistor_10 (.in(1'b0), .out(sck_pad_out), .gate(sck_clr));
  Transistor transistor_11 (.in(1'b1), .out(sck_pad_out), .gate(n_sck_set));
  Transistor #(.\type ("n")) transistor_12 (.in(1'b0), .out(transistor_12_out), .gate(transistor_6_out));
  Transistor #(.\type ("n")) transistor_13 (.in(1'b0), .out(transistor_6_out), .gate(sck_pad_in));
  Transistor #(.\type ("n")) transistor_14 (.in(transistor_15_out), .out(transistor_2_out), .gate(transistor_3_out));
  Transistor #(.\type ("n")) transistor_15 (.in(1'b0), .out(transistor_15_out), .gate(sck_pad_in));
  Pull_Resistor #(.pull(1)) pull_resistor_1 (.node(pull_resistor_1_node));
  assign controlled_buffer_1_out = undriven ? pull_resistor_1_node : 1'bz;  // Controlled_Buffer controlled_buffer_1
  not g1 (g1_out, controlled_buffer_1_out);
  nand g2 (g2_out, g3_out, controlled_buffer_1_out);
  nand g3 (g3_out, g2_out, g1_out);
  not g4 (g4_out, g3_out);

  // Notes on the sheet:
  //   g3
  //   g4
  //   g2
  //   g1
  //   ~
  //   ~
  //   _______
  //   ENA_PU
  //   SCK
  //   nand_latch
  //   nres
  //   nset
  //   nq
  //   q
  //   . . . not used
  //   ____________
  //   sck_frompad
endmodule
