// Logisim project x55.circ as structural Verilog: 1 circuit, main circuit main
module main (
  input  w13,
  input  w16,
  input  CLK2,
  input  CLK5,
  output x55
);

  wire multiplexer_1_out, nor_1_out;

  nor nor_1 (nor_1_out, w13, w16);
  Multiplexer multiplexer_1 (.in0(1'b1), .in1(nor_1_out), .out(multiplexer_1_out), .sel(CLK2));
  nor nor_2 (x55, multiplexer_1_out, CLK5);

  // Notes on the sheet:
  //   s2.op_ld_abs_rr_sx00
  //   s2.op_incdec_rr
  //   clk
  //   ~writeback
  //   s3.oe_idu_to_uhlbus
endmodule
